# Fritzing sketch AmmeterShield (saved by Fritzing 0.8.0b)
breadboards: 1

parts:
  V_R3 = Arduino
  +_CT1_- = screw terminal, 2 pins
  R11 = Resistor [tolerance=±0.1% resistance=10k package="1206 [SMD]"]
  R12 = Resistor [tolerance=±0.1% resistance=10k package="1206 [SMD]"]
  R14 = Resistor [tolerance=±0.1% resistance=10k package="1206 [SMD]"]
  R13 = Resistor [tolerance=±0.1% resistance=20k package="1206 [SMD]"]
  R15 = Resistor [tolerance=±0.1% resistance=100k package="1206 [SMD]"]
  R16 = Resistor [tolerance=±0.1% resistance=100k package="1206 [SMD]"]
  C11 = Ceramic Capacitor [capacitance=10µF voltage=10V package="1206 [SMD, multilayer]"]
  IC1 = SOIC-14 [chip_label=AD8669 package=SO]
  IC3 = SO08 [chip_label=MAX1044 package=SO]
  C01 = Electrolytic Capacitor [capacitance=10µF package="100 mil [THT, electrolytic]"]
  C02 = Electrolytic Capacitor [capacitance=10µF package="100 mil [THT, electrolytic]"]
  C03 = Ceramic Capacitor [capacitance=100nF package="1206 [SMD, multilayer]"]
  D14 = Rectifier Diode [part_number=1N4148 package="300 mil [THT]"]
  D13 = Rectifier Diode [part_number=1N4148 package="300 mil [THT]"]
  D11 = Rectifier Diode [part_number=1N4148 package="300 mil [THT]"]
  D12 = Rectifier Diode [part_number=1N4148 package="300 mil [THT]"]
  +_CT2_- = screw terminal, 2 pins
  R26 = Resistor [tolerance=±0.1% resistance=100k package="1206 [SMD]"]
  R25 = Resistor [tolerance=±0.1% resistance=100k package="1206 [SMD]"]
  R23 = Resistor [tolerance=±0.1% resistance=20k package="1206 [SMD]"]
  R24 = Resistor [tolerance=±0.1% resistance=10k package="1206 [SMD]"]
  R22 = Resistor [tolerance=±0.1% resistance=10k package="1206 [SMD]"]
  R21 = Resistor [tolerance=±0.1% resistance=10k package="1206 [SMD]"]
  C21 = Ceramic Capacitor [capacitance=10µF voltage=10V package="1206 [SMD, multilayer]"]
  D22 = Rectifier Diode [part_number=1N4148 package="300 mil [THT]"]
  D21 = Rectifier Diode [part_number=1N4148 package="300 mil [THT]"]
  D23 = Rectifier Diode [part_number=1N4148 package="300 mil [THT]"]
  D24 = Rectifier Diode [part_number=1N4148 package="300 mil [THT]"]
  R45 = Resistor [tolerance=±0.1% resistance=100k package="1206 [SMD]"]
  D44 = Rectifier Diode [part_number=1N4148 package="300 mil [THT]"]
  R33 = Resistor [tolerance=±0.1% resistance=20k package="1206 [SMD]"]
  C31 = Ceramic Capacitor [capacitance=10µF voltage=10V package="1206 [SMD, multilayer]"]
  D43 = Rectifier Diode [part_number=1N4148 package="300 mil [THT]"]
  R42 = Resistor [tolerance=±0.1% resistance=10k package="1206 [SMD]"]
  C41 = Ceramic Capacitor [capacitance=10µF voltage=10V package="1206 [SMD, multilayer]"]
  R41 = Resistor [tolerance=±0.1% resistance=10k package="1206 [SMD]"]
  R36 = Resistor [tolerance=±0.1% resistance=100k package="1206 [SMD]"]
  R32 = Resistor [tolerance=±0.1% resistance=10k package="1206 [SMD]"]
  D34 = Rectifier Diode [part_number=1N4148 package="300 mil [THT]"]
  +_CT3_- = screw terminal, 2 pins
  R43 = Resistor [tolerance=±0.1% resistance=20k package="1206 [SMD]"]
  D31 = Rectifier Diode [part_number=1N4148 package="300 mil [THT]"]
  +_CT4_- = screw terminal, 2 pins
  R35 = Resistor [tolerance=±0.1% resistance=100k package="1206 [SMD]"]
  D33 = Rectifier Diode [part_number=1N4148 package="300 mil [THT]"]
  R44 = Resistor [tolerance=±0.1% resistance=10k package="1206 [SMD]"]
  D32 = Rectifier Diode [part_number=1N4148 package="300 mil [THT]"]
  D27 = Rectifier Diode [part_number=1N4148 package="300 mil [THT]"]
  R46 = Resistor [tolerance=±0.1% resistance=100k package="1206 [SMD]"]
  D42 = Rectifier Diode [part_number=1N4148 package="300 mil [THT]"]
  R34 = Resistor [tolerance=±0.1% resistance=10k package="1206 [SMD]"]
  R31 = Resistor [tolerance=±0.1% resistance=10k package="1206 [SMD]"]
  IC2 = SOIC-14 [chip_label=AD8669 package=SO]

nets:
  GND: V_R3.GND, +_CT1_-.pin2, R16.Pin_0, C11.0, IC1.3, IC1.5, IC1.10, IC1.12, IC3.3, IC3.6, C02.+, C03.0, +_CT2_-.pin2, R26.Pin_0, C21.0, C31.0, C41.0, R36.Pin_0, +_CT3_-.pin2, +_CT4_-.pin2, R46.Pin_0, IC2.3, IC2.5, IC2.10, IC2.12
  3.3V: V_R3.3V3, IC1.4, IC3.8, C03.1, IC2.4
  CT1 Vout: V_R3.A0, R15.Pin_1, R16.Pin_1, C11.1, D14.cathode
  CT2 Vout: V_R3.A1, R26.Pin_1, R25.Pin_1, C21.1, D24.cathode
  CT3 Vout: V_R3.A2, C31.1, R36.Pin_1, D34.cathode, R35.Pin_1
  CT4 Vout: V_R3.A3, R45.Pin_1, D44.cathode, C41.1, R46.Pin_1
  N1: +_CT1_-.pin1, R11.Pin_0, R13.Pin_0
  N2: R11.Pin_1, R12.Pin_0, IC1.2, D11.cathode
  N3: R12.Pin_1, R14.Pin_0, D12.anode
  N4: R14.Pin_1, R13.Pin_1, R15.Pin_0, IC1.13, D13.anode
  N5: IC1.1, D11.anode, D12.cathode
  N6: IC1.6, R25.Pin_0, R23.Pin_1, R24.Pin_1, D23.anode
  N7: IC1.7, D23.cathode, D24.anode
  N8: IC1.8, D22.cathode, D21.anode
  N9: IC1.9, R22.Pin_0, R21.Pin_1, D21.cathode
  -3.3V Supply: IC1.11, IC3.5, C02.-, IC2.11
  N10: IC1.14, D14.anode, D13.cathode
  N11: IC3.2, C01.+
  N12: IC3.4, C01.-
  N13: +_CT2_-.pin1, R23.Pin_0, R21.Pin_0
  N14: R24.Pin_0, R22.Pin_1, D22.anode
  N15: R45.Pin_0, D43.anode, R43.Pin_1, R44.Pin_1, IC2.6
  N16: D44.anode, D43.cathode, IC2.7
  N17: R33.Pin_0, +_CT3_-.pin1, R31.Pin_0
  N18: R33.Pin_1, R35.Pin_0, D33.anode, R34.Pin_1, IC2.13
  N19: R42.Pin_0, R41.Pin_1, D27.cathode, IC2.9
  N20: R42.Pin_1, R44.Pin_0, D42.anode
  N21: R41.Pin_0, R43.Pin_0, +_CT4_-.pin1
  N22: R32.Pin_0, D31.cathode, R31.Pin_1, IC2.2
  N23: R32.Pin_1, D32.anode, R34.Pin_0
  N24: D34.anode, D33.cathode, IC2.14
  N25: D31.anode, D32.cathode, IC2.1
  N26: D27.anode, D42.cathode, IC2.8

notes:
  Version 1C
  Precision Ammeter
  Precision Ammeter Shield
  for Adruino Due (3.3V) Version 2A (06-2013)
